# Fritzing sketch esp8266-light-level-sensor-connection (saved by Fritzing 0.9.3b)

parts:
  Part1 = Adafruit TSL2561 [part_number="Adafruit #439"]

nets:
  3.3V: Part1.VIN
  GND: Part1.GND
  D1: Part1.SDA
  D2: Part1.SCL

custom parts:
  Adafruit TSL2561: The TSL2561 luminosity sensor is an advanced digital light sensor, ideal for use in a wide range of light situations. Compared to low cost CdS cells, this sensor is more precise, allowing for exact lux calculations and can be configured for different gain/timing ranges to detect light ranges from up to 0.1 - 40,000+ Lux on the fly. The best part of this sensor is that it contains both infrared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
