# Fritzing sketch esp8266-moisture-sensor-connection (saved by Fritzing 0.9.3b)

parts:
  NodeMCU_ESP8266 = Adafruit HUZZAH ESP8266 Breakout [part_number=2471]
  YL-38 = Soil Moisture Sensor
  Q1 = NPN-Transistor [package="TO92 [THT]"]
  R1 = Resistor [tolerance=±5% resistance=1k package=THT]

nets:
  N1: NodeMCU_ESP8266.A, YL-38.SIG
  N2: NodeMCU_ESP8266.#15, R1.Pin_1
  N3: NodeMCU_ESP8266.3V, Q1.C
  GND: NodeMCU_ESP8266.GND, YL-38.GND
  N4: YL-38.VCC, Q1.E
  N5: Q1.B, R1.Pin_0
