# Fritzing sketch power_module (saved by Fritzing 0.9.3b)
breadboards: 1

parts:
  TP4056_Charger = TP4056 [chip_label=TP4056 package="DIP (Dual Inline) [THT]"]
  part = Solar Panel [package="Renogy 50 Watts 12 Volt Monocrystalline Bendable Solar Panel"]
  D1 = Diode [package=diode-1n4001]
  Fuel_Gauge = MAX1704X [package=tdfn-8]
  Lipo_800mah = Battery Holders [package=lipo-1100mAh]

nets:
  N1: TP4056_Charger.pin1, D1.C
  N2: TP4056_Charger.pin2, part.Connector_2
  N3: TP4056_Charger.pin3, Fuel_Gauge.VDD
  N4: TP4056_Charger.pin4, Fuel_Gauge.CELL, Lipo_800mah.+
  N5: TP4056_Charger.pin5, Fuel_Gauge.CTG, Lipo_800mah.-
  N6: TP4056_Charger.pin6, Fuel_Gauge.GND
  N7: part.Connector_1, D1.A
  SCL ESP8266: Fuel_Gauge.SCL
  SDA ESP8266: Fuel_Gauge.SDA

custom parts:
  TP4056: A DIP stand-in part for whatever IC you want. With 6 pins on a 300mil dual inline package (DIP) footprint.
  Solar Panel: Renogy 50 Watts 12 Volt Solar Panel
