# Fritzing sketch rain_counter_module (saved by Fritzing 0.9.3b)
breadboards: 1

parts:
  U1 = attiny85 [package=dip]
  R1 = Resistor [tolerance=±5% resistance=10k package="0402 [SMD]"]
  S1 = Square Pushbutton

nets:
  N1: U1.Pin_3, R1.Pin_1, S1.leg0
  GND: U1.Pin_4, R1.Pin_0
  D1 - SDA ESP8266: U1.Pin_5
  D3 - ESP8266: U1.Pin_6
  D2 - SCL ESP8266: U1.Pin_7
  3.3V: U1.Pin_8, S1.leg1

notes:
  rain collector
