# Fritzing sketch esp8266-temperature-humidity-sensor-connection (saved by Fritzing 0.9.3b)

parts:
  NodeMCU_ESP8266 = Adafruit HUZZAH ESP8266 Breakout [part_number=2471]
  DHT1 = DHT11 Humitidy and Temperature Sensor

nets:
  N1: NodeMCU_ESP8266.#5, DHT1.DATA
  N2: NodeMCU_ESP8266.3V, DHT1.VDD
  GND: NodeMCU_ESP8266.GND, DHT1.GND

custom parts:
  DHT11 Humitidy and Temperature Sensor: DHT11 Humidity and Temperature Sensor
